// Logisim project cpu.circ as structural Verilog: 11 circuits, main circuit main
module main (
  input  RESET,
  input  [31:0] INTERRUPT_MSG,
  input  INTERRUPT
);

  wire CLK, control_unit_1_alu_oe, control_unit_1_alu_swin, control_unit_1_alu_write,
       control_unit_1_instrreg_write, control_unit_1_int_reset, control_unit_1_pc_next_out,
       control_unit_1_pc_write, control_unit_1_ram_a_ofst_1, control_unit_1_ram_a_ofst_r,
       control_unit_1_ram_a_write, control_unit_1_ram_oe, control_unit_1_ram_we, control_unit_1_regs_oe,
       control_unit_1_sp_pop, control_unit_1_sp_push, control_unit_1_sp_write, or_1_out,
       registers_array_1_interrupt;
  wire [1:0] control_unit_1_pc_cmd, control_unit_1_pc_isize, control_unit_1_ram_a_select,
       control_unit_1_regs_mode;
  wire [3:0] control_unit_1_alu_oper, control_unit_1_alu_shfa, control_unit_1_regs_sela,
       control_unit_1_regs_selb;
  wire [7:0] alu_1_flags;
  wire [15:0] bit_extender_1_out;
  wire [31:0] adder_1_out, ADDRESS_REGISTER_stored, controlled_buffer_2_out, INSTRUCTION_REGISTER_stored,
       INTERRUPT_REG_stored, multiplexer_1_out, multiplexer_2_out, PROGRAM_COUNTER_address,
       PROGRAM_COUNTER_next_address, registers_array_1_out_a, registers_array_1_out_b, STACK_POINTER_address;

  or or_1 (or_1_out, INTERRUPT, control_unit_1_int_reset);
  Multiplexer #(.width(32)) multiplexer_1 (
    .in0(INTERRUPT_MSG), .in1({32{1'b0}}), .out(multiplexer_1_out), .sel(control_unit_1_int_reset));
  REGISTER32b INTERRUPT_REG (
    .DATA(multiplexer_1_out), .WRITE(or_1_out), .CLOCK(CLK), .RESET(RESET), .STORED(INTERRUPT_REG_stored));
  Clock clock_1 (.out(CLK));
  REGISTERS_ARRAY registers_array_1 (
    .DATA(registers_array_1_out_a), .MODE(control_unit_1_regs_mode), .SELECT_A(control_unit_1_regs_sela),
    .SELECT_B(control_unit_1_regs_selb), .OUT_ENABLE(control_unit_1_regs_oe), .CLOCK(CLK), .RESET(RESET),
    .STORED_15(INTERRUPT_REG_stored), .OUT_A(registers_array_1_out_a), .OUT_B(registers_array_1_out_b),
    .INTERRUPT(registers_array_1_interrupt));
  assign registers_array_1_out_a = control_unit_1_pc_next_out ? PROGRAM_COUNTER_next_address : 32'bz;  // Controlled_Buffer controlled_buffer_1
  COUNTER32b PROGRAM_COUNTER (
    .JUMP_ADDRESS(registers_array_1_out_a), .INSTRUCTION_SIZE(control_unit_1_pc_isize),
    .CMD(control_unit_1_pc_cmd), .WRITE(control_unit_1_pc_write), .CLOCK(CLK), .RESET(RESET),
    .ADDRESS(PROGRAM_COUNTER_address), .NEXT_ADDRESS(PROGRAM_COUNTER_next_address));
  POINTER32b STACK_POINTER (
    .PUSH(control_unit_1_sp_push), .POP(control_unit_1_sp_pop), .WRITE(control_unit_1_sp_write), .CLOCK(CLK),
    .RESET(RESET), .ADDRESS(STACK_POINTER_address));
  Multiplexer #(.select(2), .width(32)) multiplexer_2 (
    .in0(PROGRAM_COUNTER_address), .in1(registers_array_1_out_a), .in2(STACK_POINTER_address),
    .out(multiplexer_2_out), .sel(control_unit_1_ram_a_select));  // open: in3
  REGISTER32b INSTRUCTION_REGISTER (
    .DATA(registers_array_1_out_a), .WRITE(control_unit_1_instrreg_write), .CLOCK(CLK), .RESET(RESET),
    .STORED(INSTRUCTION_REGISTER_stored));
  assign controlled_buffer_2_out = control_unit_1_ram_a_ofst_1 ? 32'h1 : 32'bz;  // Controlled_Buffer controlled_buffer_2
  Pull_Resistor pull_resistor_1 (.node(controlled_buffer_2_out));
  ALU alu_1 (
    .INPUT_A(registers_array_1_out_a), .INPUT_B(registers_array_1_out_b),
    .OPERATION(control_unit_1_alu_oper), .SHFA(control_unit_1_alu_shfa), .WRITE(control_unit_1_alu_write),
    .OE(control_unit_1_alu_oe), .SWITCH_INS(control_unit_1_alu_swin), .CLOCK(CLK), .RESET(RESET),
    .RESULT(registers_array_1_out_a), .FLAGS(alu_1_flags));
  assign controlled_buffer_2_out = control_unit_1_ram_a_ofst_r ? registers_array_1_out_b : 32'bz;  // Controlled_Buffer controlled_buffer_3
  Adder #(.width(32)) adder_1 (
    .a(controlled_buffer_2_out), .b(ADDRESS_REGISTER_stored), .out(adder_1_out), .cin(1'b0));  // open: cout
  REGISTER32b ADDRESS_REGISTER (
    .DATA(multiplexer_2_out), .WRITE(control_unit_1_ram_a_write), .CLOCK(CLK), .RESET(RESET),
    .STORED(ADDRESS_REGISTER_stored));
  RAM #(.addrWidth(16), .dataWidth(32), .databus("bidir")) ram_1 (
    .addr(bit_extender_1_out), .we(control_unit_1_ram_we), .oe(control_unit_1_ram_oe), .clk(CLK),
    .data(registers_array_1_out_a));
  Bit_Extender #(.in_width(32), .\type ("zero")) bit_extender_1 (.in(adder_1_out), .out(bit_extender_1_out));
  CONTROL_UNIT control_unit_1 (
    .FLAGS(alu_1_flags), .INTERRUPT(registers_array_1_interrupt), .CLOCK(CLK), .RESET(RESET),
    .INSTR(INSTRUCTION_REGISTER_stored), .RAM_OE(control_unit_1_ram_oe),
    .RAM_A_OFST_R(control_unit_1_ram_a_ofst_r), .RAM_A_OFST_1(control_unit_1_ram_a_ofst_1),
    .RAM_A_WRITE(control_unit_1_ram_a_write), .RAM_A_SELECT(control_unit_1_ram_a_select),
    .PC_NEXT_OUT(control_unit_1_pc_next_out), .PC_ISIZE(control_unit_1_pc_isize),
    .PC_CMD(control_unit_1_pc_cmd), .PC_WRITE(control_unit_1_pc_write), .SP_PUSH(control_unit_1_sp_push),
    .SP_POP(control_unit_1_sp_pop), .SP_WRITE(control_unit_1_sp_write), .INT_RESET(control_unit_1_int_reset),
    .REGS_MODE(control_unit_1_regs_mode), .REGS_SELA(control_unit_1_regs_sela),
    .REGS_SELB(control_unit_1_regs_selb), .REGS_OE(control_unit_1_regs_oe),
    .ALU_OPER(control_unit_1_alu_oper), .ALU_SHFA(control_unit_1_alu_shfa),
    .ALU_WRITE(control_unit_1_alu_write), .ALU_OE(control_unit_1_alu_oe), .ALU_SWIN(control_unit_1_alu_swin),
    .INSTRREG_WRITE(control_unit_1_instrreg_write), .RAM_WE(control_unit_1_ram_we));
endmodule

module RAM_CONTROLLER (
  input  [31:0] WRITEIN,
  input  [20:0] ADDRESS,
  input  WRITESTART,
  input  READSTART,
  input  CLK,
  output [31:0] READOUT
);

  wire and_1_out, and_2_out, and_3_out, d_ff_1_q, d_ff_2_q, d_ff_5_q, demultiplexer_1_out0,
       demultiplexer_1_out1, demultiplexer_2_out0, demultiplexer_2_out1, demultiplexer_2_out2,
       demultiplexer_2_out3, multiplexer_1_out, not_1_out, not_2_out, or_1_out, s_r_ff_1_q, xor_1_out,
       xor_2_out, xor_3_out;
  wire [1:0] d_ff_3_q;
  wire [7:0] multiplexer_2_out, RAM1_data;
  wire [20:0] adder_1_out;

  D_Flip_Flop d_ff_1 (.D(WRITESTART), .clk(CLK), .Q(d_ff_1_q));  // open: Qn, preset, reset
  D_Flip_Flop d_ff_2 (.D(READSTART), .clk(CLK), .Q(d_ff_2_q));  // open: Qn, preset, reset
  and and_1 (and_1_out, WRITESTART, not_1_out);
  not not_1 (not_1_out, d_ff_1_q);
  and and_2 (and_2_out, READSTART, not_2_out);
  not not_2 (not_2_out, d_ff_2_q);
  or or_1 (or_1_out, and_1_out, and_2_out);
  Multiplexer multiplexer_1 (.in0(d_ff_5_q), .in1(and_2_out), .out(multiplexer_1_out), .sel(or_1_out));
  D_Flip_Flop d_ff_3 (.D(xor_1_out), .clk(CLK), .Q(d_ff_3_q[0]), .reset(xor_3_out));  // open: Qn, preset
  xor xor_1 (xor_1_out, d_ff_3_q[0], 1'b1);
  D_Flip_Flop d_ff_4 (.D(xor_2_out), .clk(CLK), .Q(d_ff_3_q[1]), .reset(xor_3_out));  // open: Qn, preset
  xor xor_2 (xor_2_out, d_ff_3_q[1], d_ff_3_q[0]);
  Adder #(.width(21)) adder_1 (.a({{19{1'b0}}, d_ff_3_q}), .b(ADDRESS), .out(adder_1_out), .cin(1'b0));  // open: cout
  S_R_Flip_Flop s_r_ff_1 (.S(or_1_out), .R(and_3_out), .clk(CLK), .Q(s_r_ff_1_q));  // open: reset, Qn, preset
  D_Flip_Flop d_ff_5 (.D(multiplexer_1_out), .clk(CLK), .Q(d_ff_5_q));  // open: Qn, preset, reset
  xor xor_3 (xor_3_out, 1'b1, s_r_ff_1_q);
  and and_3 (and_3_out, d_ff_3_q[0], d_ff_3_q[1]);
  Demultiplexer demultiplexer_1 (
    .out0(demultiplexer_1_out0), .out1(demultiplexer_1_out1), .in(s_r_ff_1_q), .sel(d_ff_5_q));
  RAM #(.addrWidth(21), .asyncread("true"), .databus("bidir")) RAM1 (
    .addr(adder_1_out), .we(demultiplexer_1_out0), .oe(demultiplexer_1_out1), .clk(CLK), .data(RAM1_data));
  Multiplexer #(.select(2), .width(8)) multiplexer_2 (
    .in0(WRITEIN[31:24]), .in1(WRITEIN[23:16]), .in2(WRITEIN[15:8]), .in3(WRITEIN[7:0]),
    .out(multiplexer_2_out), .sel(d_ff_3_q));
  assign RAM1_data = demultiplexer_1_out0 ? multiplexer_2_out : 8'bz;  // Controlled_Buffer controlled_buffer_1
  Demultiplexer #(.select(2)) demultiplexer_2 (
    .out0(demultiplexer_2_out0), .out1(demultiplexer_2_out1), .out2(demultiplexer_2_out2),
    .out3(demultiplexer_2_out3), .in(demultiplexer_1_out1), .sel(d_ff_3_q));
  Register register_1 (.D(RAM1_data), .en(demultiplexer_2_out0), .clk(CLK), .Q(READOUT[31:24]));  // open: clr
  Register register_2 (.D(RAM1_data), .en(demultiplexer_2_out1), .clk(CLK), .Q(READOUT[23:16]));  // open: clr
  Register register_3 (.D(RAM1_data), .en(demultiplexer_2_out2), .clk(CLK), .Q(READOUT[15:8]));  // open: clr
  Register register_4 (.D(RAM1_data), .en(demultiplexer_2_out3), .clk(CLK), .Q(READOUT[7:0]));  // open: clr
endmodule

module REGISTER32b (
  input  [31:0] DATA,
  input  WRITE,
  input  CLOCK,
  input  RESET,
  output [31:0] STORED
);

  Register #(.width(32)) register_1 (.D(DATA), .en(WRITE), .clk(CLOCK), .Q(STORED), .clr(RESET));
  Hex_Digit_Display hex_digit_display_1 (.value(STORED[31:28]));  // open: dp
  Hex_Digit_Display hex_digit_display_2 (.value(STORED[27:24]));  // open: dp
  Hex_Digit_Display hex_digit_display_3 (.value(STORED[23:20]));  // open: dp
  Hex_Digit_Display hex_digit_display_4 (.value(STORED[19:16]));  // open: dp
  Hex_Digit_Display hex_digit_display_5 (.value(STORED[15:12]));  // open: dp
  Hex_Digit_Display hex_digit_display_6 (.value(STORED[11:8]));  // open: dp
  Hex_Digit_Display hex_digit_display_7 (.value(STORED[7:4]));  // open: dp
  Hex_Digit_Display hex_digit_display_8 (.value(STORED[3:0]));  // open: dp
endmodule

module COUNTER32b (
  input  [31:0] JUMP_ADDRESS,
  input  [1:0] INSTRUCTION_SIZE,
  input  [1:0] CMD,
  input  WRITE,
  input  CLOCK,
  input  RESET,
  output [31:0] ADDRESS,
  output [31:0] NEXT_ADDRESS
);

  wire [31:0] bit_extender_1_out, multiplexer_1_out;

  Adder #(.width(32)) adder_1 (.a(ADDRESS), .b(bit_extender_1_out), .out(NEXT_ADDRESS), .cin(1'b0));  // open: cout
  assign bit_extender_1_out = {{30{1'b0}}, INSTRUCTION_SIZE};  // Bit_Extender bit_extender_1
  Multiplexer #(.select(2), .width(32)) multiplexer_1 (
    .in0(ADDRESS), .in1(NEXT_ADDRESS), .in2(JUMP_ADDRESS), .in3({32{1'b0}}), .out(multiplexer_1_out),
    .sel(CMD));
  REGISTER32b register32b_1 (.DATA(multiplexer_1_out), .WRITE(WRITE), .CLOCK(CLOCK), .RESET(RESET), .STORED(ADDRESS));
endmodule

module CONTROL_UNIT (
  input  [31:0] INSTR,
  input  [7:0] FLAGS,
  input  INTERRUPT,
  input  CLOCK,
  input  RESET,
  output INSTRREG_WRITE,
  output RAM_WE,
  output RAM_OE,
  output RAM_A_OFST_R,
  output RAM_A_OFST_1,
  output RAM_A_WRITE,
  output [1:0] RAM_A_SELECT,
  output PC_NEXT_OUT,
  output [1:0] PC_ISIZE,
  output [1:0] PC_CMD,
  output PC_WRITE,
  output SP_PUSH,
  output SP_POP,
  output SP_WRITE,
  output INT_RESET,
  output [1:0] REGS_MODE,
  output [3:0] REGS_SELA,
  output [3:0] REGS_SELB,
  output REGS_OE,
  output [3:0] ALU_OPER,
  output [3:0] ALU_SHFA,
  output ALU_WRITE,
  output ALU_OE,
  output ALU_SWIN
);

  wire ALU_OP_CONST_is_on, ALU_OP_CONST_next_state, ALU_OP_is_on, ALU_OP_next_state, ALU_TO_REG_is_on,
       ALU_TO_REG_next_state, and_1_out, and_2_out, and_3_out, and_4_out, and_5_out, and_6_out, and_7_out,
       and_8_out, and_9_out, and_10_out, and_11_out, and_12_out, and_13_out, and_14_out, buffer_12_out,
       buffer_13_out, buffer_15_out, buffer_16_out, buffer_17_out, buffer_19_out, buffer_22_out,
       buffer_24_out, buffer_28_out, buffer_29_out, buffer_30_out, buffer_38_out, buffer_41_out,
       buffer_42_out, buffer_44_out, CAN_JUMP, controlled_buffer_1_out, controlled_buffer_2_out,
       controlled_buffer_3_out, controlled_buffer_4_out, controlled_buffer_5_out, controlled_buffer_6_out,
       controlled_buffer_7_out, controlled_buffer_8_out, controlled_buffer_9_out, controlled_buffer_10_out,
       controlled_buffer_11_out, controlled_buffer_12_out, controlled_buffer_13_out,
       controlled_buffer_14_out, controlled_buffer_15_out, controlled_buffer_16_out,
       controlled_buffer_17_out, controlled_buffer_18_out, DECODE, FETCH1, FETCH2, GET_NEXT_is_on,
       GET_NEXT_next_state, GET_OFFSET_is_on, GET_OFFSET_next_state, ICODE_0000, ICODE_0001, ICODE_0010,
       ICODE_0011, ICODE_0100, ICODE_1011, ISIZE_2, ITYPE_ALU, ITYPE_CTRLFLOW, ITYPE_DATA, JUMP, JUMP_IF,
       nor_10_out, not_1_out, not_2_out, not_3_out, not_4_out, not_5_out, not_6_out, not_7_out, not_8_out,
       not_9_out, not_10_out, not_11_out, not_12_out, not_13_out, not_14_out, not_15_out, not_16_out,
       not_17_out, or_1_out, POP_INCR_is_on, POP_INCR_next_state, PUSH_ADDR_is_on, PUSH_ADDR_next_state,
       PUSH_DECR_is_on, PUSH_DECR_next_state, PUSH_VALUE_is_on, PUSH_VALUE_next_state, RAM_TO_ADDR_is_on,
       RAM_TO_ADDR_next_state, RAM_TO_REG_is_on, RAM_TO_REG_next_state, REG_TO_ADDR_is_on,
       REG_TO_ADDR_next_state, REG_TO_RAM_is_on, REG_TO_RAM_next_state, REG_TO_REG_is_on,
       REG_TO_REG_next_state, RESTART, SP_SET_ADDR_is_on, SP_SET_ADDR_next_state, STEP1;
  wire [1:0] multiplexer_1_out;

  nor nor_1 (ITYPE_DATA, INSTR[31], INSTR[30], INSTR[29], not_1_out);
  not not_1 (not_1_out, INSTR[28]);
  not not_2 (not_2_out, INSTR[29]);
  nor nor_2 (ITYPE_ALU, INSTR[31], INSTR[30], not_2_out, INSTR[28]);
  not not_3 (not_3_out, INSTR[29]);
  nor nor_3 (ITYPE_CTRLFLOW, INSTR[31], INSTR[30], not_3_out, not_4_out);
  and and_1 (and_1_out, ITYPE_DATA, ICODE_0000);
  and and_2 (and_2_out, ITYPE_DATA, ICODE_0001);
  not not_4 (not_4_out, INSTR[28]);
  assign controlled_buffer_1_out = INSTR[11] ? controlled_buffer_2_out : 1'bz;  // Controlled_Buffer controlled_buffer_1
  assign controlled_buffer_2_out = and_1_out ? and_1_out : 1'bz;  // Controlled_Buffer controlled_buffer_2
  not not_5 (not_5_out, INSTR[11]);
  Pull_Resistor pull_resistor_1 (.node(controlled_buffer_2_out));
  assign controlled_buffer_3_out = not_5_out ? controlled_buffer_2_out : 1'bz;  // Controlled_Buffer controlled_buffer_3
  and and_3 (and_3_out, ITYPE_CTRLFLOW, ICODE_0000);
  assign controlled_buffer_4_out = INSTR[10] ? controlled_buffer_5_out : 1'bz;  // Controlled_Buffer controlled_buffer_4
  assign controlled_buffer_5_out = and_2_out ? and_2_out : 1'bz;  // Controlled_Buffer controlled_buffer_5
  not not_6 (not_6_out, INSTR[10]);
  Pull_Resistor pull_resistor_2 (.node(controlled_buffer_5_out));
  assign controlled_buffer_6_out = not_6_out ? controlled_buffer_5_out : 1'bz;  // Controlled_Buffer controlled_buffer_6
  and and_4 (and_4_out, ITYPE_CTRLFLOW, ICODE_0001);
  nor nor_4 (ICODE_0000, INSTR[27], INSTR[26], INSTR[25], INSTR[24]);
  assign controlled_buffer_7_out = INSTR[10] ? controlled_buffer_3_out : 1'bz;  // Controlled_Buffer controlled_buffer_7
  not not_7 (not_7_out, INSTR[10]);
  Pull_Resistor pull_resistor_3 (.node(controlled_buffer_3_out));
  assign controlled_buffer_8_out = not_7_out ? controlled_buffer_3_out : 1'bz;  // Controlled_Buffer controlled_buffer_8
  assign controlled_buffer_9_out = and_3_out ? and_3_out : 1'bz;  // Controlled_Buffer controlled_buffer_9
  and and_5 (and_5_out, ITYPE_DATA, ICODE_0010);
  assign controlled_buffer_10_out = ITYPE_ALU ? ITYPE_ALU : 1'bz;  // Controlled_Buffer controlled_buffer_10
  not not_8 (not_8_out, INSTR[11]);
  Pull_Resistor pull_resistor_4 (.node(controlled_buffer_10_out));
  assign controlled_buffer_11_out = and_4_out ? and_4_out : 1'bz;  // Controlled_Buffer controlled_buffer_11
  and and_6 (and_6_out, ITYPE_DATA, ICODE_0011);
  and and_7 (and_7_out, ITYPE_DATA, ICODE_0100);
  and and_8 (and_8_out, ITYPE_CTRLFLOW, ICODE_0010);
  and and_9 (and_9_out, ITYPE_CTRLFLOW, ICODE_0011);
  buf buffer_1 (ISIZE_2, controlled_buffer_1_out);
  buf buffer_2 (ISIZE_2, controlled_buffer_8_out);
  buf buffer_3 (JUMP, controlled_buffer_9_out);
  buf buffer_4 (ISIZE_2, controlled_buffer_9_out);
  buf buffer_5 (ISIZE_2, controlled_buffer_6_out);
  assign controlled_buffer_12_out = and_5_out ? and_5_out : 1'bz;  // Controlled_Buffer controlled_buffer_12
  assign controlled_buffer_13_out = INSTR[11] ? controlled_buffer_10_out : 1'bz;  // Controlled_Buffer controlled_buffer_13
  assign controlled_buffer_14_out = not_8_out ? controlled_buffer_10_out : 1'bz;  // Controlled_Buffer controlled_buffer_14
  buf buffer_6 (JUMP_IF, controlled_buffer_11_out);
  assign controlled_buffer_15_out = and_6_out ? and_6_out : 1'bz;  // Controlled_Buffer controlled_buffer_15
  assign controlled_buffer_16_out = and_7_out ? and_7_out : 1'bz;  // Controlled_Buffer controlled_buffer_16
  buf buffer_7 (JUMP, controlled_buffer_17_out);
  assign controlled_buffer_17_out = and_8_out ? and_8_out : 1'bz;  // Controlled_Buffer controlled_buffer_17
  assign controlled_buffer_18_out = and_9_out ? and_9_out : 1'bz;  // Controlled_Buffer controlled_buffer_18
  not not_9 (not_9_out, INSTR[24]);
  nor nor_5 (ICODE_0001, INSTR[27], INSTR[26], INSTR[25], not_9_out);
  buf buffer_8 (ISIZE_2, controlled_buffer_13_out);
  buf buffer_9 (ISIZE_2, controlled_buffer_11_out);
  buf buffer_10 (ISIZE_2, controlled_buffer_17_out);
  buf buffer_11 (JUMP, controlled_buffer_18_out);
  not not_10 (not_10_out, INSTR[25]);
  nor nor_6 (ICODE_0010, INSTR[27], INSTR[26], not_10_out, INSTR[24]);
  buf buffer_12 (buffer_12_out, controlled_buffer_13_out);
  buf buffer_13 (buffer_13_out, controlled_buffer_13_out);
  buf buffer_14 (buffer_12_out, controlled_buffer_14_out);
  buf buffer_15 (buffer_15_out, controlled_buffer_14_out);
  buf buffer_16 (buffer_16_out, controlled_buffer_15_out);
  buf buffer_17 (buffer_17_out, controlled_buffer_1_out);
  buf buffer_18 (buffer_17_out, controlled_buffer_7_out);
  buf buffer_19 (buffer_19_out, controlled_buffer_7_out);
  buf buffer_20 (buffer_17_out, controlled_buffer_8_out);
  buf buffer_21 (buffer_19_out, controlled_buffer_8_out);
  buf buffer_22 (buffer_22_out, controlled_buffer_4_out);
  buf buffer_23 (buffer_22_out, controlled_buffer_6_out);
  buf buffer_24 (buffer_24_out, controlled_buffer_12_out);
  buf buffer_25 (buffer_17_out, controlled_buffer_16_out);
  buf buffer_26 (buffer_19_out, controlled_buffer_16_out);
  buf buffer_27 (buffer_19_out, controlled_buffer_18_out);
  not not_11 (not_11_out, INSTR[25]);
  not not_12 (not_12_out, INSTR[24]);
  nor nor_7 (ICODE_0011, INSTR[27], INSTR[26], not_11_out, not_12_out);
  buf buffer_28 (buffer_28_out, controlled_buffer_1_out);
  buf buffer_29 (buffer_29_out, controlled_buffer_7_out);
  buf buffer_30 (buffer_30_out, controlled_buffer_8_out);
  buf buffer_31 (buffer_28_out, controlled_buffer_8_out);
  buf buffer_32 (buffer_28_out, controlled_buffer_9_out);
  buf buffer_33 (buffer_29_out, controlled_buffer_4_out);
  buf buffer_34 (buffer_30_out, controlled_buffer_6_out);
  buf buffer_35 (buffer_28_out, controlled_buffer_6_out);
  buf buffer_36 (buffer_28_out, controlled_buffer_13_out);
  buf buffer_37 (buffer_28_out, controlled_buffer_11_out);
  buf buffer_38 (buffer_38_out, controlled_buffer_16_out);
  buf buffer_39 (buffer_28_out, controlled_buffer_17_out);
  buf buffer_40 (buffer_38_out, controlled_buffer_18_out);
  not not_13 (not_13_out, INSTR[26]);
  nor nor_8 (ICODE_0100, INSTR[27], not_13_out, INSTR[25], INSTR[24]);
  buf buffer_41 (buffer_41_out, controlled_buffer_15_out);
  buf buffer_42 (buffer_42_out, controlled_buffer_15_out);
  buf buffer_43 (buffer_41_out, controlled_buffer_16_out);
  buf buffer_44 (buffer_44_out, controlled_buffer_17_out);
  buf buffer_45 (buffer_41_out, controlled_buffer_17_out);
  buf buffer_46 (buffer_42_out, controlled_buffer_17_out);
  buf buffer_47 (buffer_41_out, controlled_buffer_18_out);
  not not_14 (not_14_out, INSTR[27]);
  not not_15 (not_15_out, INSTR[25]);
  not not_16 (not_16_out, INSTR[24]);
  nor nor_9 (ICODE_1011, not_14_out, INSTR[26], not_15_out, not_16_out);
  D_Flip_Flop FETCH_1 (.D(RESTART), .clk(CLOCK), .Q(FETCH1), .preset(RESET), .reset(1'b0));  // open: Qn
  assign RAM_OE = FETCH1 ? 1'b1 : 1'bz;  // Controlled_Buffer controlled_buffer_19
  D_Flip_Flop FETCH_2 (.D(FETCH1), .clk(CLOCK), .Q(FETCH2), .preset(1'b0), .reset(RESET));  // open: Qn
  D_Flip_Flop u_DECODE (.D(FETCH2), .clk(CLOCK), .Q(DECODE), .preset(1'b0), .reset(RESET));  // open: Qn
  assign INSTRREG_WRITE = FETCH2 ? 1'b1 : 1'bz;  // Controlled_Buffer controlled_buffer_20
  assign RAM_OE = FETCH2 ? 1'b1 : 1'bz;  // Controlled_Buffer controlled_buffer_21
  Pull_Resistor pull_resistor_5 (.node(buffer_42_out));
  CONTROL_STATE PUSH_DECR (
    .ENABLE(buffer_42_out), .PREV_STATE(DECODE), .CLOCK(CLOCK), .RESET(RESET),
    .NEXT_STATE(PUSH_DECR_next_state), .IS_ON(PUSH_DECR_is_on));
  assign SP_PUSH = PUSH_DECR_is_on ? 1'b1 : 1'bz;  // Controlled_Buffer controlled_buffer_22
  assign SP_WRITE = PUSH_DECR_is_on ? 1'b1 : 1'bz;  // Controlled_Buffer controlled_buffer_23
  Pull_Resistor pull_resistor_6 (.node(buffer_41_out));
  CONTROL_STATE SP_SET_ADDR (
    .ENABLE(buffer_41_out), .PREV_STATE(PUSH_DECR_next_state), .CLOCK(CLOCK), .RESET(RESET),
    .NEXT_STATE(SP_SET_ADDR_next_state), .IS_ON(SP_SET_ADDR_is_on));
  LED led_1 (.in(FETCH1));
  Pull_Resistor pull_resistor_7 (.node(buffer_44_out));
  assign RAM_A_WRITE = SP_SET_ADDR_is_on ? 1'b1 : 1'bz;  // Controlled_Buffer controlled_buffer_24
  assign RAM_A_SELECT = SP_SET_ADDR_is_on ? 2'b10 : 2'bz;  // Controlled_Buffer controlled_buffer_25
  LED led_2 (.in(FETCH2));
  LED led_3 (.in(DECODE));
  JUMP_CONDITION jump_condition_1 (.FLAGS(FLAGS), .FLAG_SEL(INSTR[7:4]), .JUMP(CAN_JUMP));
  LED led_4 (.in(STEP1));
  CONTROL_STATE PUSH_ADDR (
    .ENABLE(buffer_44_out), .PREV_STATE(SP_SET_ADDR_next_state), .CLOCK(CLOCK), .RESET(RESET),
    .NEXT_STATE(PUSH_ADDR_next_state), .IS_ON(PUSH_ADDR_is_on));
  assign RAM_WE = PUSH_ADDR_is_on ? 1'b1 : 1'bz;  // Controlled_Buffer controlled_buffer_26
  assign RAM_A_WRITE = PUSH_ADDR_is_on ? 1'b1 : 1'bz;  // Controlled_Buffer controlled_buffer_27
  assign PC_NEXT_OUT = PUSH_ADDR_is_on ? 1'b1 : 1'bz;  // Controlled_Buffer controlled_buffer_28
  LED led_5 (.in(RESTART));
  Pull_Resistor pull_resistor_8 (.node(buffer_28_out));
  LED led_6 (.in(nor_10_out));
  nor nor_10 (nor_10_out, FETCH1, FETCH2, DECODE, STEP1, RESTART);
  Pull_Resistor pull_resistor_9 (.node(buffer_30_out));
  CONTROL_STATE GET_NEXT (
    .ENABLE(buffer_28_out), .PREV_STATE(PUSH_ADDR_next_state), .CLOCK(CLOCK), .RESET(RESET),
    .NEXT_STATE(GET_NEXT_next_state), .IS_ON(GET_NEXT_is_on));
  assign RAM_OE = GET_NEXT_is_on ? 1'b1 : 1'bz;  // Controlled_Buffer controlled_buffer_29
  assign RAM_A_OFST_1 = GET_NEXT_is_on ? 1'b1 : 1'bz;  // Controlled_Buffer controlled_buffer_30
  CONTROL_STATE RAM_TO_ADDR (
    .ENABLE(buffer_30_out), .PREV_STATE(GET_NEXT_next_state), .CLOCK(CLOCK), .RESET(RESET),
    .NEXT_STATE(RAM_TO_ADDR_next_state), .IS_ON(RAM_TO_ADDR_is_on));
  Pull_Resistor pull_resistor_10 (.node(buffer_29_out));
  assign RAM_OE = RAM_TO_ADDR_is_on ? 1'b1 : 1'bz;  // Controlled_Buffer controlled_buffer_31
  assign RAM_A_WRITE = RAM_TO_ADDR_is_on ? 1'b1 : 1'bz;  // Controlled_Buffer controlled_buffer_32
  assign RAM_A_SELECT = RAM_TO_ADDR_is_on ? 2'b01 : 2'bz;  // Controlled_Buffer controlled_buffer_33
  CONTROL_STATE REG_TO_ADDR (
    .ENABLE(buffer_29_out), .PREV_STATE(RAM_TO_ADDR_next_state), .CLOCK(CLOCK), .RESET(RESET),
    .NEXT_STATE(REG_TO_ADDR_next_state), .IS_ON(REG_TO_ADDR_is_on));
  assign RAM_A_WRITE = REG_TO_ADDR_is_on ? 1'b1 : 1'bz;  // Controlled_Buffer controlled_buffer_34
  assign RAM_A_SELECT = REG_TO_ADDR_is_on ? 2'b01 : 2'bz;  // Controlled_Buffer controlled_buffer_35
  assign REGS_SELA = REG_TO_ADDR_is_on ? INSTR[19:16] : 4'bz;  // Controlled_Buffer controlled_buffer_36
  assign REGS_OE = REG_TO_ADDR_is_on ? 1'b1 : 1'bz;  // Controlled_Buffer controlled_buffer_37
  Pull_Resistor pull_resistor_11 (.node(buffer_38_out));
  CONTROL_STATE POP_INCR (
    .ENABLE(buffer_38_out), .PREV_STATE(REG_TO_ADDR_next_state), .CLOCK(CLOCK), .RESET(RESET),
    .NEXT_STATE(POP_INCR_next_state), .IS_ON(POP_INCR_is_on));
  Pull_Resistor pull_resistor_12 (.node(buffer_19_out));
  assign SP_POP = POP_INCR_is_on ? 1'b1 : 1'bz;  // Controlled_Buffer controlled_buffer_38
  assign SP_WRITE = POP_INCR_is_on ? 1'b1 : 1'bz;  // Controlled_Buffer controlled_buffer_39
  and and_10 (and_10_out, INSTR[9], GET_OFFSET_is_on);
  assign RAM_A_OFST_R = and_10_out ? 1'b1 : 1'bz;  // Controlled_Buffer controlled_buffer_40
  assign REGS_MODE = and_10_out ? 2'b01 : 2'bz;  // Controlled_Buffer controlled_buffer_41
  assign REGS_SELB = and_10_out ? INSTR[15:12] : 4'bz;  // Controlled_Buffer controlled_buffer_42
  assign REGS_OE = and_10_out ? 1'b1 : 1'bz;  // Controlled_Buffer controlled_buffer_43
  CONTROL_STATE GET_OFFSET (
    .ENABLE(buffer_19_out), .PREV_STATE(POP_INCR_next_state), .CLOCK(CLOCK), .RESET(RESET),
    .NEXT_STATE(GET_OFFSET_next_state), .IS_ON(GET_OFFSET_is_on));
  assign RAM_OE = GET_OFFSET_is_on ? 1'b1 : 1'bz;  // Controlled_Buffer controlled_buffer_44
  Pull_Resistor pull_resistor_13 (.node(buffer_17_out));
  CONTROL_STATE RAM_TO_REG (
    .ENABLE(buffer_17_out), .PREV_STATE(GET_OFFSET_next_state), .CLOCK(CLOCK), .RESET(RESET),
    .NEXT_STATE(RAM_TO_REG_next_state), .IS_ON(RAM_TO_REG_is_on));
  assign RAM_OE = RAM_TO_REG_is_on ? 1'b1 : 1'bz;  // Controlled_Buffer controlled_buffer_45
  assign REGS_MODE = RAM_TO_REG_is_on ? 2'b11 : 2'bz;  // Controlled_Buffer controlled_buffer_46
  assign REGS_SELB = RAM_TO_REG_is_on ? INSTR[23:20] : 4'bz;  // Controlled_Buffer controlled_buffer_47
  Pull_Resistor pull_resistor_14 (.node(buffer_22_out));
  and and_11 (and_11_out, INSTR[9], REG_TO_RAM_is_on);
  assign RAM_A_OFST_R = and_11_out ? 1'b1 : 1'bz;  // Controlled_Buffer controlled_buffer_48
  assign REGS_SELB = and_11_out ? INSTR[15:12] : 4'bz;  // Controlled_Buffer controlled_buffer_49
  CONTROL_STATE REG_TO_RAM (
    .ENABLE(buffer_22_out), .PREV_STATE(RAM_TO_REG_next_state), .CLOCK(CLOCK), .RESET(RESET),
    .NEXT_STATE(REG_TO_RAM_next_state), .IS_ON(REG_TO_RAM_is_on));
  Pull_Resistor pull_resistor_15 (.node(buffer_24_out));
  assign RAM_WE = REG_TO_RAM_is_on ? 1'b1 : 1'bz;  // Controlled_Buffer controlled_buffer_50
  assign REGS_SELA = REG_TO_RAM_is_on ? INSTR[23:20] : 4'bz;  // Controlled_Buffer controlled_buffer_51
  assign REGS_OE = REG_TO_RAM_is_on ? 1'b1 : 1'bz;  // Controlled_Buffer controlled_buffer_52
  CONTROL_STATE REG_TO_REG (
    .ENABLE(buffer_24_out), .PREV_STATE(REG_TO_RAM_next_state), .CLOCK(CLOCK), .RESET(RESET),
    .NEXT_STATE(REG_TO_REG_next_state), .IS_ON(REG_TO_REG_is_on));
  assign REGS_MODE = REG_TO_REG_is_on ? 2'b10 : 2'bz;  // Controlled_Buffer controlled_buffer_53
  assign REGS_SELA = REG_TO_REG_is_on ? INSTR[23:20] : 4'bz;  // Controlled_Buffer controlled_buffer_54
  assign REGS_SELB = REG_TO_REG_is_on ? INSTR[19:16] : 4'bz;  // Controlled_Buffer controlled_buffer_55
  Pull_Resistor pull_resistor_16 (.node(buffer_15_out));
  Pull_Resistor pull_resistor_17 (.node(buffer_13_out));
  CONTROL_STATE ALU_OP (
    .ENABLE(buffer_15_out), .PREV_STATE(REG_TO_REG_next_state), .CLOCK(CLOCK), .RESET(RESET),
    .NEXT_STATE(ALU_OP_next_state), .IS_ON(ALU_OP_is_on));
  assign REGS_SELA = ALU_OP_is_on ? INSTR[23:20] : 4'bz;  // Controlled_Buffer controlled_buffer_56
  assign REGS_SELB = ALU_OP_is_on ? INSTR[19:16] : 4'bz;  // Controlled_Buffer controlled_buffer_57
  assign REGS_OE = ALU_OP_is_on ? 1'b1 : 1'bz;  // Controlled_Buffer controlled_buffer_58
  assign ALU_OPER = ALU_OP_is_on ? INSTR[27:24] : 4'bz;  // Controlled_Buffer controlled_buffer_59
  assign ALU_SHFA = ALU_OP_is_on ? INSTR[7:4] : 4'bz;  // Controlled_Buffer controlled_buffer_60
  assign ALU_WRITE = ALU_OP_is_on ? 1'b1 : 1'bz;  // Controlled_Buffer controlled_buffer_61
  CONTROL_STATE ALU_OP_CONST (
    .ENABLE(buffer_13_out), .PREV_STATE(ALU_OP_next_state), .CLOCK(CLOCK), .RESET(RESET),
    .NEXT_STATE(ALU_OP_CONST_next_state), .IS_ON(ALU_OP_CONST_is_on));
  Pull_Resistor pull_resistor_18 (.node(buffer_12_out));
  assign RAM_OE = ALU_OP_CONST_is_on ? 1'b1 : 1'bz;  // Controlled_Buffer controlled_buffer_62
  assign REGS_MODE = ALU_OP_CONST_is_on ? 2'b01 : 2'bz;  // Controlled_Buffer controlled_buffer_63
  assign REGS_SELB = ALU_OP_CONST_is_on ? INSTR[23:20] : 4'bz;  // Controlled_Buffer controlled_buffer_64
  assign REGS_OE = ALU_OP_CONST_is_on ? 1'b1 : 1'bz;  // Controlled_Buffer controlled_buffer_65
  assign ALU_OPER = ALU_OP_CONST_is_on ? INSTR[27:24] : 4'bz;  // Controlled_Buffer controlled_buffer_66
  Controlled_Buffer #(.width(4)) controlled_buffer_67 (.out(ALU_SHFA), .en(ALU_OP_CONST_is_on));  // open: in
  assign ALU_WRITE = ALU_OP_CONST_is_on ? 1'b1 : 1'bz;  // Controlled_Buffer controlled_buffer_68
  assign ALU_SWIN = ALU_OP_CONST_is_on ? INSTR[10] : 1'bz;  // Controlled_Buffer controlled_buffer_69
  CONTROL_STATE ALU_TO_REG (
    .ENABLE(buffer_12_out), .PREV_STATE(ALU_OP_CONST_next_state), .CLOCK(CLOCK), .RESET(RESET),
    .NEXT_STATE(ALU_TO_REG_next_state), .IS_ON(ALU_TO_REG_is_on));
  not not_17 (not_17_out, ICODE_1011);
  and and_12 (and_12_out, not_17_out, ALU_TO_REG_is_on);
  assign REGS_MODE = and_12_out ? 2'b11 : 2'bz;  // Controlled_Buffer controlled_buffer_70
  assign REGS_SELB = and_12_out ? INSTR[15:12] : 4'bz;  // Controlled_Buffer controlled_buffer_71
  assign ALU_OE = and_12_out ? 1'b1 : 1'bz;  // Controlled_Buffer controlled_buffer_72
  Pull_Resistor pull_resistor_19 (.node(buffer_16_out));
  Pull_Resistor pull_resistor_20 (.node(JUMP_IF));
  CONTROL_STATE PUSH_VALUE (
    .ENABLE(buffer_16_out), .PREV_STATE(ALU_TO_REG_next_state), .CLOCK(CLOCK), .RESET(RESET),
    .NEXT_STATE(PUSH_VALUE_next_state), .IS_ON(PUSH_VALUE_is_on));
  assign RAM_WE = PUSH_VALUE_is_on ? 1'b1 : 1'bz;  // Controlled_Buffer controlled_buffer_73
  assign REGS_SELA = PUSH_VALUE_is_on ? INSTR[23:20] : 4'bz;  // Controlled_Buffer controlled_buffer_74
  assign REGS_OE = PUSH_VALUE_is_on ? 1'b1 : 1'bz;  // Controlled_Buffer controlled_buffer_75
  Pull_Resistor pull_resistor_21 (.node(JUMP));
  and and_13 (and_13_out, JUMP_IF, CAN_JUMP);
  or or_1 (or_1_out, and_13_out, JUMP);
  and and_14 (and_14_out, or_1_out, STEP1);
  assign RAM_OE = and_14_out ? 1'b1 : 1'bz;  // Controlled_Buffer controlled_buffer_76
  D_Flip_Flop STEP_1 (.D(PUSH_VALUE_next_state), .clk(CLOCK), .Q(STEP1), .preset(1'b0), .reset(RESET));  // open: Qn
  Multiplexer #(.width(2)) multiplexer_1 (.in0(2'b01), .in1(2'b10), .out(multiplexer_1_out), .sel(and_14_out));
  D_Flip_Flop STEP_2 (.D(STEP1), .clk(CLOCK), .Q(RESTART), .preset(1'b0), .reset(RESET));  // open: Qn
  assign PC_CMD = STEP1 ? multiplexer_1_out : 2'bz;  // Controlled_Buffer controlled_buffer_77
  assign PC_WRITE = STEP1 ? 1'b1 : 1'bz;  // Controlled_Buffer controlled_buffer_78
  assign RAM_A_WRITE = RESTART ? 1'b1 : 1'bz;  // Controlled_Buffer controlled_buffer_79
  Pull_Resistor pull_resistor_22 (.node(INSTRREG_WRITE));
  Pull_Resistor pull_resistor_23 (.node(RAM_WE));
  Pull_Resistor pull_resistor_24 (.node(RAM_OE));
  Pull_Resistor pull_resistor_25 (.node(RAM_A_OFST_R));
  Pull_Resistor pull_resistor_26 (.node(RAM_A_OFST_1));
  Pull_Resistor pull_resistor_27 (.node(RAM_A_WRITE));
  Pull_Resistor pull_resistor_28 (.node(RAM_A_SELECT));
  Pull_Resistor pull_resistor_29 (.node(PC_NEXT_OUT));
  Pull_Resistor pull_resistor_30 (.node(ISIZE_2));
  Pull_Resistor pull_resistor_31 (.node(PC_ISIZE));
  Multiplexer #(.width(2)) multiplexer_2 (.in0(2'b01), .in1(2'b10), .out(PC_ISIZE), .sel(ISIZE_2));
  Pull_Resistor pull_resistor_32 (.node(PC_CMD));
  Pull_Resistor pull_resistor_33 (.node(PC_WRITE));
  Pull_Resistor pull_resistor_34 (.node(SP_PUSH));
  Pull_Resistor pull_resistor_35 (.node(SP_POP));
  Pull_Resistor pull_resistor_36 (.node(SP_WRITE));
  Pull_Resistor pull_resistor_37 (.node(INT_RESET));
  Pull_Resistor pull_resistor_38 (.node(REGS_MODE));
  Pull_Resistor pull_resistor_39 (.node(REGS_SELA));
  Pull_Resistor pull_resistor_40 (.node(REGS_SELB));
  Pull_Resistor pull_resistor_41 (.node(REGS_OE));
  Pull_Resistor pull_resistor_42 (.node(ALU_OPER));
  Pull_Resistor pull_resistor_43 (.node(ALU_SHFA));
  Pull_Resistor pull_resistor_44 (.node(ALU_WRITE));
  Pull_Resistor pull_resistor_45 (.node(ALU_OE));
  Pull_Resistor pull_resistor_46 (.node(ALU_SWIN));

  // Other names for the same wires on the sheet: SHFA_FLAGS[3:0] = INSTR[7:4]; IS_REG3 = INSTR[8];
  //   OFST_REG = INSTR[9]; ADDR_REG = INSTR[10]; CONST = INSTR[11]; REG3[3:0] = INSTR[15:12];
  //   REG2[3:0] = INSTR[19:16]; REG1[3:0] = INSTR[23:20]; ICODE[3:0] = INSTR[27:24]; CLK = CLOCK; STEP2 = RESTART

  // Notes on the sheet:
  //   LOAD
  //   STORE
  //   JUMP
  //   JUMP_IF
  //   MOVE
  //   PUSH
  //   POP
  //   CALL
  //   RETURN
  //   OPTIONAL LINE FOR OFFSET
  //   OPTIONAL LINE FOR OFFSET
endmodule

module REGISTERS_ARRAY (
  input  [31:0] DATA,
  input  [1:0] MODE,
  input  [3:0] SELECT_A,
  input  [3:0] SELECT_B,
  input  OUT_ENABLE,
  input  CLOCK,
  input  RESET,
  input  [31:0] STORED_15,
  output [31:0] OUT_A,
  output [31:0] OUT_B,
  output INTERRUPT
);

  wire decoder_1_out0, decoder_1_out2, decoder_1_out3, decoder_3_out0, decoder_3_out1, decoder_3_out2,
       decoder_3_out3, decoder_3_out4, decoder_3_out5, decoder_3_out6, decoder_3_out7, decoder_3_out8,
       decoder_3_out9, decoder_3_out10, decoder_3_out11, decoder_3_out12, decoder_3_out13, decoder_3_out14,
       decoder_3_out15, or_1_out, or_2_out;
  wire [15:0] decoder_2_out0, pull_resistor_1_node;
  wire [31:0] controlled_buffer_2_out, controlled_buffer_18_out, multiplexer_1_out, register32b_1_stored,
       register32b_2_stored, register32b_3_stored, register32b_4_stored, register32b_5_stored,
       register32b_6_stored, register32b_7_stored, register32b_8_stored, register32b_9_stored,
       register32b_10_stored, register32b_11_stored, register32b_12_stored, register32b_13_stored,
       register32b_14_stored, register32b_15_stored;

  Decoder #(.select(2)) decoder_1 (
    .out0(decoder_1_out0), .out2(decoder_1_out2), .out3(decoder_1_out3), .sel(MODE));  // open: out1, en
  or or_1 (or_1_out, decoder_1_out0, decoder_1_out2);
  Decoder #(.select(4)) decoder_2 (
    .out0(decoder_2_out0[0]), .out1(decoder_2_out0[1]), .out2(decoder_2_out0[2]), .out3(decoder_2_out0[3]),
    .out4(decoder_2_out0[4]), .out5(decoder_2_out0[5]), .out6(decoder_2_out0[6]), .out7(decoder_2_out0[7]),
    .out8(decoder_2_out0[8]), .out9(decoder_2_out0[9]), .out10(decoder_2_out0[10]),
    .out11(decoder_2_out0[11]), .out12(decoder_2_out0[12]), .out13(decoder_2_out0[13]),
    .out14(decoder_2_out0[14]), .out15(decoder_2_out0[15]), .sel(SELECT_B));  // open: en
  Multiplexer #(.width(32)) multiplexer_1 (
    .in0(controlled_buffer_2_out), .in1(DATA), .out(multiplexer_1_out), .sel(decoder_1_out3));
  or or_2 (or_2_out, decoder_1_out2, decoder_1_out3);
  Pull_Resistor pull_resistor_1 (.node(pull_resistor_1_node));
  assign pull_resistor_1_node = or_2_out ? decoder_2_out0 : 16'bz;  // Controlled_Buffer controlled_buffer_1
  Decoder #(.select(4)) decoder_3 (
    .out0(decoder_3_out0), .out1(decoder_3_out1), .out2(decoder_3_out2), .out3(decoder_3_out3),
    .out4(decoder_3_out4), .out5(decoder_3_out5), .out6(decoder_3_out6), .out7(decoder_3_out7),
    .out8(decoder_3_out8), .out9(decoder_3_out9), .out10(decoder_3_out10), .out11(decoder_3_out11),
    .out12(decoder_3_out12), .out13(decoder_3_out13), .out14(decoder_3_out14), .out15(decoder_3_out15),
    .sel(SELECT_A), .en(or_1_out));
  assign controlled_buffer_2_out = decoder_3_out0 ? register32b_1_stored : 32'bz;  // Controlled_Buffer controlled_buffer_2
  REGISTER32b register32b_1 (
    .DATA(multiplexer_1_out), .WRITE(pull_resistor_1_node[0]), .CLOCK(CLOCK), .RESET(RESET),
    .STORED(register32b_1_stored));
  REGISTER32b register32b_2 (
    .DATA(multiplexer_1_out), .WRITE(pull_resistor_1_node[1]), .CLOCK(CLOCK), .RESET(RESET),
    .STORED(register32b_2_stored));
  REGISTER32b register32b_3 (
    .DATA(multiplexer_1_out), .WRITE(pull_resistor_1_node[2]), .CLOCK(CLOCK), .RESET(RESET),
    .STORED(register32b_3_stored));
  REGISTER32b register32b_4 (
    .DATA(multiplexer_1_out), .WRITE(pull_resistor_1_node[3]), .CLOCK(CLOCK), .RESET(RESET),
    .STORED(register32b_4_stored));
  REGISTER32b register32b_5 (
    .DATA(multiplexer_1_out), .WRITE(pull_resistor_1_node[4]), .CLOCK(CLOCK), .RESET(RESET),
    .STORED(register32b_5_stored));
  REGISTER32b register32b_6 (
    .DATA(multiplexer_1_out), .WRITE(pull_resistor_1_node[5]), .CLOCK(CLOCK), .RESET(RESET),
    .STORED(register32b_6_stored));
  REGISTER32b register32b_7 (
    .DATA(multiplexer_1_out), .WRITE(pull_resistor_1_node[6]), .CLOCK(CLOCK), .RESET(RESET),
    .STORED(register32b_7_stored));
  REGISTER32b register32b_8 (
    .DATA(multiplexer_1_out), .WRITE(pull_resistor_1_node[7]), .CLOCK(CLOCK), .RESET(RESET),
    .STORED(register32b_8_stored));
  REGISTER32b register32b_9 (
    .DATA(multiplexer_1_out), .WRITE(pull_resistor_1_node[8]), .CLOCK(CLOCK), .RESET(RESET),
    .STORED(register32b_9_stored));
  REGISTER32b register32b_10 (
    .DATA(multiplexer_1_out), .WRITE(pull_resistor_1_node[9]), .CLOCK(CLOCK), .RESET(RESET),
    .STORED(register32b_10_stored));
  REGISTER32b register32b_11 (
    .DATA(multiplexer_1_out), .WRITE(pull_resistor_1_node[10]), .CLOCK(CLOCK), .RESET(RESET),
    .STORED(register32b_11_stored));
  REGISTER32b register32b_12 (
    .DATA(multiplexer_1_out), .WRITE(pull_resistor_1_node[11]), .CLOCK(CLOCK), .RESET(RESET),
    .STORED(register32b_12_stored));
  REGISTER32b register32b_13 (
    .DATA(multiplexer_1_out), .WRITE(pull_resistor_1_node[12]), .CLOCK(CLOCK), .RESET(RESET),
    .STORED(register32b_13_stored));
  REGISTER32b register32b_14 (
    .DATA(multiplexer_1_out), .WRITE(pull_resistor_1_node[13]), .CLOCK(CLOCK), .RESET(RESET),
    .STORED(register32b_14_stored));
  REGISTER32b register32b_15 (
    .DATA(multiplexer_1_out), .WRITE(pull_resistor_1_node[14]), .CLOCK(CLOCK), .RESET(RESET),
    .STORED(register32b_15_stored));
  assign controlled_buffer_2_out = decoder_3_out1 ? register32b_2_stored : 32'bz;  // Controlled_Buffer controlled_buffer_3
  assign controlled_buffer_2_out = decoder_3_out2 ? register32b_3_stored : 32'bz;  // Controlled_Buffer controlled_buffer_4
  assign controlled_buffer_2_out = decoder_3_out3 ? register32b_4_stored : 32'bz;  // Controlled_Buffer controlled_buffer_5
  assign controlled_buffer_2_out = decoder_3_out4 ? register32b_5_stored : 32'bz;  // Controlled_Buffer controlled_buffer_6
  assign controlled_buffer_2_out = decoder_3_out5 ? register32b_6_stored : 32'bz;  // Controlled_Buffer controlled_buffer_7
  assign controlled_buffer_2_out = decoder_3_out6 ? register32b_7_stored : 32'bz;  // Controlled_Buffer controlled_buffer_8
  assign controlled_buffer_2_out = decoder_3_out7 ? register32b_8_stored : 32'bz;  // Controlled_Buffer controlled_buffer_9
  assign controlled_buffer_2_out = decoder_3_out8 ? register32b_9_stored : 32'bz;  // Controlled_Buffer controlled_buffer_10
  assign controlled_buffer_2_out = decoder_3_out9 ? register32b_10_stored : 32'bz;  // Controlled_Buffer controlled_buffer_11
  assign controlled_buffer_2_out = decoder_3_out10 ? register32b_11_stored : 32'bz;  // Controlled_Buffer controlled_buffer_12
  assign controlled_buffer_2_out = decoder_3_out11 ? register32b_12_stored : 32'bz;  // Controlled_Buffer controlled_buffer_13
  assign controlled_buffer_2_out = decoder_3_out12 ? register32b_13_stored : 32'bz;  // Controlled_Buffer controlled_buffer_14
  assign controlled_buffer_2_out = decoder_3_out13 ? register32b_14_stored : 32'bz;  // Controlled_Buffer controlled_buffer_15
  assign controlled_buffer_2_out = decoder_3_out14 ? register32b_15_stored : 32'bz;  // Controlled_Buffer controlled_buffer_16
  assign controlled_buffer_2_out = decoder_3_out15 ? STORED_15 : 32'bz;  // Controlled_Buffer controlled_buffer_17
  assign controlled_buffer_18_out = decoder_2_out0[0] ? register32b_1_stored : 32'bz;  // Controlled_Buffer controlled_buffer_18
  assign controlled_buffer_18_out = decoder_2_out0[1] ? register32b_2_stored : 32'bz;  // Controlled_Buffer controlled_buffer_19
  assign controlled_buffer_18_out = decoder_2_out0[2] ? register32b_3_stored : 32'bz;  // Controlled_Buffer controlled_buffer_20
  assign controlled_buffer_18_out = decoder_2_out0[3] ? register32b_4_stored : 32'bz;  // Controlled_Buffer controlled_buffer_21
  assign controlled_buffer_18_out = decoder_2_out0[4] ? register32b_5_stored : 32'bz;  // Controlled_Buffer controlled_buffer_22
  assign controlled_buffer_18_out = decoder_2_out0[5] ? register32b_6_stored : 32'bz;  // Controlled_Buffer controlled_buffer_23
  assign controlled_buffer_18_out = decoder_2_out0[6] ? register32b_7_stored : 32'bz;  // Controlled_Buffer controlled_buffer_24
  assign controlled_buffer_18_out = decoder_2_out0[7] ? register32b_8_stored : 32'bz;  // Controlled_Buffer controlled_buffer_25
  assign controlled_buffer_18_out = decoder_2_out0[8] ? register32b_9_stored : 32'bz;  // Controlled_Buffer controlled_buffer_26
  assign controlled_buffer_18_out = decoder_2_out0[9] ? register32b_10_stored : 32'bz;  // Controlled_Buffer controlled_buffer_27
  assign controlled_buffer_18_out = decoder_2_out0[10] ? register32b_11_stored : 32'bz;  // Controlled_Buffer controlled_buffer_28
  assign controlled_buffer_18_out = decoder_2_out0[11] ? register32b_12_stored : 32'bz;  // Controlled_Buffer controlled_buffer_29
  assign controlled_buffer_18_out = decoder_2_out0[12] ? register32b_13_stored : 32'bz;  // Controlled_Buffer controlled_buffer_30
  assign controlled_buffer_18_out = decoder_2_out0[13] ? register32b_14_stored : 32'bz;  // Controlled_Buffer controlled_buffer_31
  assign controlled_buffer_18_out = decoder_2_out0[14] ? register32b_15_stored : 32'bz;  // Controlled_Buffer controlled_buffer_32
  assign controlled_buffer_18_out = decoder_2_out0[15] ? STORED_15 : 32'bz;  // Controlled_Buffer controlled_buffer_33
  assign OUT_A = OUT_ENABLE ? controlled_buffer_2_out : 32'bz;  // Controlled_Buffer controlled_buffer_34
  assign OUT_B = OUT_ENABLE ? controlled_buffer_18_out : 32'bz;  // Controlled_Buffer controlled_buffer_35

  assign INTERRUPT = STORED_15[0];

  // Other names for the same wires on the sheet: CLK = CLOCK; OE = OUT_ENABLE

  // Notes on the sheet:
  //   0
  //   1
  //   2
  //   3
  //   4
  //   5
  //   6
  //   7
  //   8
  //   9
  //   10
  //   11
  //   12
  //   13
  //   14
endmodule

module CONTROL_STATE (
  input  ENABLE,
  input  PREV_STATE,
  input  CLOCK,
  input  RESET,
  output NEXT_STATE,
  output IS_ON
);

  wire and_1_out, and_2_out, not_1_out;

  not not_1 (not_1_out, ENABLE);
  and and_1 (and_1_out, not_1_out, PREV_STATE);
  D_Flip_Flop d_ff_1 (.D(and_2_out), .clk(CLOCK), .Q(IS_ON), .preset(1'b0), .reset(RESET));  // open: Qn
  and and_2 (and_2_out, ENABLE, PREV_STATE);
  or or_1 (NEXT_STATE, and_1_out, IS_ON);
endmodule

module ALU (
  input  [31:0] INPUT_A,
  input  [31:0] INPUT_B,
  input  [3:0] OPERATION,
  input  [3:0] SHFA,
  input  WRITE,
  input  OE,
  input  SWITCH_INS,
  input  CLOCK,
  input  RESET,
  output [31:0] RESULT,
  output [7:0] FLAGS
);

  wire decoder_1_out0, decoder_1_out1, decoder_1_out2, decoder_1_out3, decoder_1_out4, decoder_1_out5,
       decoder_1_out6, decoder_1_out7, decoder_1_out8, decoder_1_out9, decoder_1_out10, decoder_1_out11,
       not_1_out, or_1_out;
  wire [4:0] bit_extender_1_out;
  wire [31:0] ACCUMULATOR_stored, adder_1_out, and_1_out, controlled_buffer_1_out, divider_1_out,
       divider_1_rem, multiplexer_1_out, multiplexer_2_out, multiplier_1_out, not_2_out, or_2_out,
       shifter_1_out, shifter_2_out, subtractor_1_out, xor_1_out;

  assign bit_extender_1_out = {{1{1'b0}}, SHFA};  // Bit_Extender bit_extender_1
  Multiplexer #(.width(32)) multiplexer_1 (.in0(INPUT_B), .in1(INPUT_A), .out(multiplexer_1_out), .sel(not_1_out));
  not not_1 (not_1_out, SWITCH_INS);
  Multiplexer #(.width(32)) multiplexer_2 (.in0(INPUT_A), .in1(INPUT_B), .out(multiplexer_2_out), .sel(not_1_out));
  Decoder #(.select(4)) decoder_1 (
    .out0(decoder_1_out0), .out1(decoder_1_out1), .out2(decoder_1_out2), .out3(decoder_1_out3),
    .out4(decoder_1_out4), .out5(decoder_1_out5), .out6(decoder_1_out6), .out7(decoder_1_out7),
    .out8(decoder_1_out8), .out9(decoder_1_out9), .out10(decoder_1_out10), .out11(decoder_1_out11),
    .sel(OPERATION));  // open: out12, out13, out14, out15, en
  or or_1 (or_1_out, decoder_1_out11, decoder_1_out1);
  assign controlled_buffer_1_out = decoder_1_out0 ? adder_1_out : 32'bz;  // Controlled_Buffer controlled_buffer_1
  Adder #(.width(32)) adder_1 (
    .a(multiplexer_1_out), .b(multiplexer_2_out), .out(adder_1_out), .cin(1'b0));  // open: cout
  assign controlled_buffer_1_out = or_1_out ? subtractor_1_out : 32'bz;  // Controlled_Buffer controlled_buffer_2
  Subtractor #(.width(32)) subtractor_1 (
    .a(multiplexer_1_out), .b(multiplexer_2_out), .out(subtractor_1_out), .bin(1'b0));  // open: bout
  assign controlled_buffer_1_out = decoder_1_out2 ? multiplier_1_out : 32'bz;  // Controlled_Buffer controlled_buffer_3
  Multiplier #(.mode("twosComplement"), .width(32)) multiplier_1 (
    .a(multiplexer_1_out), .b(multiplexer_2_out), .out(multiplier_1_out), .cin({32{1'b0}}));  // open: cout
  assign controlled_buffer_1_out = decoder_1_out3 ? divider_1_out : 32'bz;  // Controlled_Buffer controlled_buffer_4
  Divider #(.mode("twosComplement"), .width(32)) divider_1 (
    .a(multiplexer_1_out), .b(multiplexer_2_out), .out(divider_1_out), .upper({32{1'b0}}), .rem(divider_1_rem));
  assign controlled_buffer_1_out = decoder_1_out4 ? divider_1_rem : 32'bz;  // Controlled_Buffer controlled_buffer_5
  assign and_1_out = multiplexer_1_out & multiplexer_2_out;  // AND_Gate and_1, 32 bits wide
  assign controlled_buffer_1_out = decoder_1_out5 ? and_1_out : 32'bz;  // Controlled_Buffer controlled_buffer_6
  assign or_2_out = multiplexer_1_out | multiplexer_2_out;  // OR_Gate or_2, 32 bits wide
  assign controlled_buffer_1_out = decoder_1_out6 ? or_2_out : 32'bz;  // Controlled_Buffer controlled_buffer_7
  assign not_2_out = ~multiplexer_1_out;  // NOT_Gate not_2, 32 bits wide
  assign controlled_buffer_1_out = decoder_1_out7 ? not_2_out : 32'bz;  // Controlled_Buffer controlled_buffer_8
  assign xor_1_out = multiplexer_1_out ^ multiplexer_2_out;  // XOR_Gate xor_1, 32 bits wide
  assign controlled_buffer_1_out = decoder_1_out8 ? xor_1_out : 32'bz;  // Controlled_Buffer controlled_buffer_9
  assign controlled_buffer_1_out = decoder_1_out9 ? shifter_1_out : 32'bz;  // Controlled_Buffer controlled_buffer_10
  Shifter #(.width(32)) shifter_1 (.in(multiplexer_1_out), .\dist (bit_extender_1_out), .out(shifter_1_out));
  assign controlled_buffer_1_out = decoder_1_out10 ? shifter_2_out : 32'bz;  // Controlled_Buffer controlled_buffer_11
  Shifter #(.shift("lr"), .width(32)) shifter_2 (
    .in(multiplexer_1_out), .\dist (bit_extender_1_out), .out(shifter_2_out));
  REGISTER32b ACCUMULATOR (
    .DATA(controlled_buffer_1_out), .WRITE(WRITE), .CLOCK(CLOCK), .RESET(RESET), .STORED(ACCUMULATOR_stored));
  assign RESULT = OE ? ACCUMULATOR_stored : 32'bz;  // Controlled_Buffer controlled_buffer_12
  FLAGS_GEN flags_gen_1 (.VALUE(ACCUMULATOR_stored), .FLAGS(FLAGS));
endmodule

module FLAGS_GEN (
  input  [31:0] VALUE,
  output [7:0] FLAGS
);

  nor nor_1 (FLAGS[0], VALUE[0], VALUE[1], VALUE[2], VALUE[3], VALUE[4], VALUE[5], VALUE[6], VALUE[7], VALUE[8], VALUE[9], VALUE[10], VALUE[11], VALUE[12], VALUE[13], VALUE[14], VALUE[15], VALUE[17], VALUE[18], VALUE[19], VALUE[20], VALUE[21], VALUE[22], VALUE[23], VALUE[24], VALUE[25], VALUE[26], VALUE[27], VALUE[28], VALUE[29], VALUE[30], VALUE[31], VALUE[16]);
  not not_1 (FLAGS[1], FLAGS[0]);
  not not_2 (FLAGS[2], VALUE[31]);
  not not_3 (FLAGS[4], FLAGS[3]);
  not not_4 (FLAGS[6], VALUE[0]);
  or or_1 (FLAGS[3], FLAGS[0], VALUE[31]);

  assign {FLAGS[7], FLAGS[5]} = {VALUE[0], VALUE[31]};
endmodule

module JUMP_CONDITION (
  input  [7:0] FLAGS,
  input  [3:0] FLAG_SEL,
  output JUMP
);

  wire [2:0] bit_extender_1_out;

  BitSelector bitselector_1 (.in(FLAGS), .out(JUMP), .sel(bit_extender_1_out));
  Bit_Extender #(.in_width(4), .out_width(3), .\type ("zero")) bit_extender_1 (.in(FLAG_SEL), .out(bit_extender_1_out));
endmodule

module POINTER32b (
  input  PUSH,
  input  POP,
  input  WRITE,
  input  CLOCK,
  input  RESET,
  output [31:0] ADDRESS
);

  wire [31:0] adder_1_out, controlled_buffer_1_out;

  assign controlled_buffer_1_out = PUSH ? {32{1'b1}} : 32'bz;  // Controlled_Buffer controlled_buffer_1
  assign controlled_buffer_1_out = POP ? 32'h1 : 32'bz;  // Controlled_Buffer controlled_buffer_2
  Pull_Resistor pull_resistor_1 (.node(controlled_buffer_1_out));
  Adder #(.width(32)) adder_1 (.a(ADDRESS), .b(controlled_buffer_1_out), .out(adder_1_out), .cin(1'b0));  // open: cout
  REGISTER32b register32b_1 (.DATA(adder_1_out), .WRITE(WRITE), .CLOCK(CLOCK), .RESET(RESET), .STORED(ADDRESS));
endmodule
